# Fritzing sketch ARDUINO_BLUETOOTH_REMOTE_CIRCUIT_DIAGRAM (saved by Fritzing 0.9.3b)
breadboards: 1

parts:
  Part1 = Arduino Uno (Rev3) - ICSP
  M1 = DC Motor
  M2 = DC Motor
  Part2 = Bluetooth HC-05 Macho
  IC1 = L293D [package=THT]
  VCC1 = Battery block 9V

nets:
  N1: Part1.D9_PWM, IC1.Enable_2
  N2: Part1.D10_PWM/SS, IC1.In_4
  N3: Part1.D11_PWM/MOSI, IC1.In_2
  N4: Part1.D12/MISO, IC1.In_1
  N5: Part1.D0/RX, Part2.TXD
  N6: Part1.D1/TX, Part2.RXD
  5V: Part1.5V, Part2.VCC, IC1.+V
  GND: Part1.GND, Part2.GND, IC1.0V, VCC1.-
  N7: M1.pin_1, IC1.Out_3_(_Controlled_by_Enable_2_)
  N8: M1.pin_2, IC1.Out_4_(_Controlled_by_Enable_2_)
  N9: M2.pin_1, IC1.Out_2_(_Controlled_by_Enable_1_)
  N10: M2.pin_2, IC1.Out_1_(_Controlled_by_Enable_1_)
  N11: IC1.+Vmotor, VCC1.+
